// Logisim project projectB.circ as structural Verilog: 5 circuits, main circuit main
module main (
);

  wire [31:0] videocarta_1_out_5, videocarta_1_out_6, videocarta_1_out_7, videocarta_1_out_8,
       videocarta_1_out_9, videocarta_1_out_10, videocarta_1_out_11, videocarta_1_out_12,
       videocarta_1_out_13, videocarta_1_out_14, videocarta_1_out_15, videocarta_1_out_16,
       videocarta_1_out_17, videocarta_1_out_18, videocarta_1_out_19, videocarta_1_out_20,
       videocarta_1_out_21, videocarta_1_out_22, videocarta_1_out_23, videocarta_1_out_24,
       videocarta_1_out_25, videocarta_1_out_26, videocarta_1_out_27, videocarta_1_out_28,
       videocarta_1_out_29, videocarta_1_out_30, videocarta_1_out_31, videocarta_1_out_32,
       videocarta_1_out_33, videocarta_1_out_34, videocarta_1_out_35, videocarta_1_out_36;

  score score_1 ();  // open: restart, рядом_справа, x, рядом_слева, out_5, out_6
  DotMatrix #(.matrixcols(32), .matrixrows(32)) dotmatrix_1 (
    .col0(videocarta_1_out_5), .col1(videocarta_1_out_6), .col2(videocarta_1_out_7),
    .col3(videocarta_1_out_8), .col4(videocarta_1_out_9), .col5(videocarta_1_out_10),
    .col6(videocarta_1_out_11), .col7(videocarta_1_out_12), .col8(videocarta_1_out_13),
    .col9(videocarta_1_out_14), .col10(videocarta_1_out_15), .col11(videocarta_1_out_16),
    .col12(videocarta_1_out_17), .col13(videocarta_1_out_18), .col14(videocarta_1_out_19),
    .col15(videocarta_1_out_20), .col16(videocarta_1_out_21), .col17(videocarta_1_out_22),
    .col18(videocarta_1_out_23), .col19(videocarta_1_out_24), .col20(videocarta_1_out_25),
    .col21(videocarta_1_out_26), .col22(videocarta_1_out_27), .col23(videocarta_1_out_28),
    .col24(videocarta_1_out_29), .col25(videocarta_1_out_30), .col26(videocarta_1_out_31),
    .col27(videocarta_1_out_32), .col28(videocarta_1_out_33), .col29(videocarta_1_out_34),
    .col30(videocarta_1_out_35), .col31(videocarta_1_out_36));
  videocarta videocarta_1 (
    .out_5(videocarta_1_out_5), .out_6(videocarta_1_out_6), .out_7(videocarta_1_out_7),
    .out_8(videocarta_1_out_8), .out_9(videocarta_1_out_9), .out_10(videocarta_1_out_10),
    .out_11(videocarta_1_out_11), .out_12(videocarta_1_out_12), .out_13(videocarta_1_out_13),
    .out_14(videocarta_1_out_14), .out_15(videocarta_1_out_15), .out_16(videocarta_1_out_16),
    .out_17(videocarta_1_out_17), .out_18(videocarta_1_out_18), .out_19(videocarta_1_out_19),
    .out_20(videocarta_1_out_20), .out_21(videocarta_1_out_21), .out_22(videocarta_1_out_22),
    .out_23(videocarta_1_out_23), .out_24(videocarta_1_out_24), .out_25(videocarta_1_out_25),
    .out_26(videocarta_1_out_26), .out_27(videocarta_1_out_27), .out_28(videocarta_1_out_28),
    .out_29(videocarta_1_out_29), .out_30(videocarta_1_out_30), .out_31(videocarta_1_out_31),
    .out_32(videocarta_1_out_32), .out_33(videocarta_1_out_33), .out_34(videocarta_1_out_34),
    .out_35(videocarta_1_out_35), .out_36(videocarta_1_out_36));  // open: y, x, palka_left, palka_right
endmodule

module videocarta (
  input  [31:0] palka_left,
  input  [31:0] y,
  input  [31:0] x,
  input  [31:0] palka_right,
  output [31:0] out_5,
  output [31:0] out_6,
  output [31:0] out_7,
  output [31:0] out_8,
  output [31:0] out_9,
  output [31:0] out_10,
  output [31:0] out_11,
  output [31:0] out_12,
  output [31:0] out_13,
  output [31:0] out_14,
  output [31:0] out_15,
  output [31:0] out_16,
  output [31:0] out_17,
  output [31:0] out_18,
  output [31:0] out_19,
  output [31:0] out_20,
  output [31:0] out_21,
  output [31:0] out_22,
  output [31:0] out_23,
  output [31:0] out_24,
  output [31:0] out_25,
  output [31:0] out_26,
  output [31:0] out_27,
  output [31:0] out_28,
  output [31:0] out_29,
  output [31:0] out_30,
  output [31:0] out_31,
  output [31:0] out_32,
  output [31:0] out_33,
  output [31:0] out_34,
  output [31:0] out_35,
  output [31:0] out_36
);

  wire [31:0] multiplexer_1_out, multiplexer_32_out;

  Multiplexer #(.width(32), .enable("false")) multiplexer_1 (
    .in0({32{1'b0}}), .in1(y), .out(multiplexer_1_out), .sel(x[0]));
  Multiplexer #(.width(32), .enable("false")) multiplexer_2 (.in0({32{1'b0}}), .in1(y), .out(out_10), .sel(x[1]));
  Multiplexer #(.width(32), .enable("false")) multiplexer_3 (.in0({32{1'b0}}), .in1(y), .out(out_9), .sel(x[2]));
  Multiplexer #(.width(32), .enable("false")) multiplexer_4 (.in0({32{1'b0}}), .in1(y), .out(out_12), .sel(x[3]));
  Multiplexer #(.width(32), .enable("false")) multiplexer_5 (.in0({32{1'b0}}), .in1(y), .out(out_14), .sel(x[4]));
  Multiplexer #(.width(32), .enable("false")) multiplexer_6 (.in0({32{1'b0}}), .in1(y), .out(out_16), .sel(x[5]));
  Multiplexer #(.width(32), .enable("false")) multiplexer_7 (.in0({32{1'b0}}), .in1(y), .out(out_17), .sel(x[6]));
  Multiplexer #(.width(32), .enable("false")) multiplexer_8 (.in0({32{1'b0}}), .in1(y), .out(out_20), .sel(x[7]));
  Multiplexer #(.width(32), .enable("false")) multiplexer_9 (.in0({32{1'b0}}), .in1(y), .out(out_22), .sel(x[8]));
  Multiplexer #(.width(32), .enable("false")) multiplexer_10 (.in0({32{1'b0}}), .in1(y), .out(out_25), .sel(x[9]));
  Multiplexer #(.width(32), .enable("false")) multiplexer_11 (.in0({32{1'b0}}), .in1(y), .out(out_26), .sel(x[10]));
  Multiplexer #(.width(32), .enable("false")) multiplexer_12 (.in0({32{1'b0}}), .in1(y), .out(out_28), .sel(x[11]));
  Multiplexer #(.width(32), .enable("false")) multiplexer_13 (.in0({32{1'b0}}), .in1(y), .out(out_31), .sel(x[12]));
  Multiplexer #(.width(32), .enable("false")) multiplexer_14 (.in0({32{1'b0}}), .in1(y), .out(out_32), .sel(x[13]));
  Multiplexer #(.width(32), .enable("false")) multiplexer_15 (.in0({32{1'b0}}), .in1(y), .out(out_34), .sel(x[14]));
  Multiplexer #(.width(32), .enable("false")) multiplexer_16 (.in0({32{1'b0}}), .in1(y), .out(out_35), .sel(x[15]));
  assign out_6 = palka_left | multiplexer_1_out;  // OR_Gate or_1, 32 bits wide
  Multiplexer #(.width(32), .enable("false")) multiplexer_17 (.in0({32{1'b0}}), .in1(y), .out(out_5), .sel(x[16]));
  Multiplexer #(.width(32), .enable("false")) multiplexer_18 (.in0({32{1'b0}}), .in1(y), .out(out_7), .sel(x[17]));
  Multiplexer #(.width(32), .enable("false")) multiplexer_19 (.in0({32{1'b0}}), .in1(y), .out(out_8), .sel(x[18]));
  Multiplexer #(.width(32), .enable("false")) multiplexer_20 (.in0({32{1'b0}}), .in1(y), .out(out_11), .sel(x[19]));
  Multiplexer #(.width(32), .enable("false")) multiplexer_21 (.in0({32{1'b0}}), .in1(y), .out(out_13), .sel(x[20]));
  Multiplexer #(.width(32), .enable("false")) multiplexer_22 (.in0({32{1'b0}}), .in1(y), .out(out_15), .sel(x[21]));
  Multiplexer #(.width(32), .enable("false")) multiplexer_23 (.in0({32{1'b0}}), .in1(y), .out(out_18), .sel(x[22]));
  Multiplexer #(.width(32), .enable("false")) multiplexer_24 (.in0({32{1'b0}}), .in1(y), .out(out_19), .sel(x[23]));
  Multiplexer #(.width(32), .enable("false")) multiplexer_25 (.in0({32{1'b0}}), .in1(y), .out(out_21), .sel(x[24]));
  Multiplexer #(.width(32), .enable("false")) multiplexer_26 (.in0({32{1'b0}}), .in1(y), .out(out_23), .sel(x[25]));
  Multiplexer #(.width(32), .enable("false")) multiplexer_27 (.in0({32{1'b0}}), .in1(y), .out(out_24), .sel(x[26]));
  Multiplexer #(.width(32), .enable("false")) multiplexer_28 (.in0({32{1'b0}}), .in1(y), .out(out_27), .sel(x[27]));
  Multiplexer #(.width(32), .enable("false")) multiplexer_29 (.in0({32{1'b0}}), .in1(y), .out(out_29), .sel(x[28]));
  Multiplexer #(.width(32), .enable("false")) multiplexer_30 (.in0({32{1'b0}}), .in1(y), .out(out_30), .sel(x[29]));
  Multiplexer #(.width(32), .enable("false")) multiplexer_31 (.in0({32{1'b0}}), .in1(y), .out(out_33), .sel(x[30]));
  Multiplexer #(.width(32), .enable("false")) multiplexer_32 (
    .in0({32{1'b0}}), .in1(y), .out(multiplexer_32_out), .sel(x[31]));
  assign out_36 = multiplexer_32_out | palka_right;  // OR_Gate or_2, 32 bits wide
endmodule

module score (
  input  [31:0] x,
  output restart,
  output \рядом_справа ,
  output \рядом_слева ,
  output [3:0] out_5,
  output [3:0] out_6
);

  wire comparator_1_eq, comparator_2_eq, comparator_3_eq, comparator_4_eq, comparator_5_eq, comparator_6_eq,
       or_1_out, or_2_out, or_3_out, or_4_out;
  wire [3:0] adder_1_out, adder_2_out;

  or or_1 (or_1_out, 1'b0, or_2_out);
  Adder #(.width(4)) adder_1 (.a(out_5), .b(4'b0001), .out(adder_1_out));  // open: cin, cout
  Register #(.width(4)) register_1 (.D(adder_1_out), .en(1'b1), .Q(out_5), .clk(comparator_4_eq), .clr(or_1_out));
  Comparator #(.width(4)) comparator_1 (.a(out_5), .b(4'b1111), .eq(comparator_1_eq));  // open: gt, lt
  or or_2 (or_2_out, comparator_1_eq, comparator_2_eq);
  or or_3 (or_3_out, or_4_out, or_2_out);
  Adder #(.width(4)) adder_2 (.a(out_6), .b(4'b0001), .out(adder_2_out));  // open: cin, cout
  Comparator #(.width(4)) comparator_2 (.a(out_6), .b(4'b1111), .eq(comparator_2_eq));  // open: gt, lt
  Register #(.width(4)) register_2 (.D(adder_2_out), .en(1'b1), .Q(out_6), .clk(comparator_3_eq), .clr(or_1_out));
  Comparator #(.width(32)) comparator_3 (.a(x), .b(32'h80000000), .eq(comparator_3_eq));  // open: gt, lt
  Comparator #(.width(32)) comparator_4 (.a(x), .b(32'h1), .eq(comparator_4_eq));  // open: gt, lt
  Comparator #(.width(32)) comparator_5 (.a(x), .b(32'h40000000), .eq(comparator_5_eq));  // open: gt, lt
  Comparator #(.width(32)) comparator_6 (.a(x), .b(32'h2), .eq(comparator_6_eq));  // open: gt, lt
  or or_4 (or_4_out, comparator_3_eq, comparator_4_eq);
endmodule

module rocketka (
);

  Subtractor subtractor_1 ();  // open: a, b, out, bin, bout
  Adder adder_1 ();  // open: a, b, out, cin, cout
endmodule

module x (
  input  reset,
  input  hit,
  output [31:0] out_3
);

  wire clock_1_out, comparator_1_eq, comparator_2_eq, multiplexer_1_out, not_1_out, or_1_out, random_1_out,
       register_1_q;
  wire [0:0] xor_1_out;
  wire [4:0] adder_1_out, multiplexer_2_out, register_2_q, subtractor_1_out;

  Comparator #(.width(5)) comparator_1 (.a({5{1'b1}}), .b(register_2_q), .eq(comparator_1_eq));  // open: gt, lt
  Comparator #(.width(5)) comparator_2 (.a({5{1'b0}}), .b(register_2_q), .eq(comparator_2_eq));  // open: gt, lt
  or or_1 (or_1_out, comparator_1_eq, comparator_2_eq, hit, reset);
  Random #(.width(1)) random_1 (.next(1'b1), .out(random_1_out), .clr(1'b0));  // open: clk
  Register #(.width(1)) register_1 (
    .D(multiplexer_1_out), .en(or_1_out), .Q(register_1_q), .clk(clock_1_out), .clr(1'b0));
  Clock clock_1 (.out(clock_1_out));
  not not_1 (not_1_out, register_1_q);
  Multiplexer #(.select(2), .enable("false")) multiplexer_1 (
    .in0(not_1_out), .in1(random_1_out), .in2(register_1_q), .in3(register_1_q), .out(multiplexer_1_out),
    .sel({1'b0, reset}));
  xor xor_1 (xor_1_out[0], register_1_q, or_1_out);
  Shifter #(.width(32)) shifter_1 (.in(32'h1), .\dist (register_2_q), .out(out_3));
  Multiplexer #(.select(2), .width(5), .enable("false")) multiplexer_2 (
    .in0(subtractor_1_out), .in1(adder_1_out), .in2(5'b01111), .in3(5'b01111), .out(multiplexer_2_out));  // open: sel
  Register #(.width(5)) register_2 (
    .D(multiplexer_2_out), .en(1'b1), .Q(register_2_q), .clk(clock_1_out));  // open: clr
  Adder #(.width(5)) adder_1 (.a(register_2_q), .b(5'b00001), .out(adder_1_out));  // open: cin, cout
  Subtractor #(.width(5)) subtractor_1 (.a(register_2_q), .b(5'b00001), .out(subtractor_1_out));  // open: bin, bout
endmodule
